# Fritzing sketch Wiring (saved by Fritzing 1.0.1rc)
breadboards: 1

parts:
  Part1 = Arduino Uno (Rev3)
  LCD2 = Serial Enabled 16x2 LCD - Black on Green 5V [part_number=LCD-09393]
  U1 = ESP8266 ESP-01 Upgraded WiFi Module [part_number=ESP8266]
  R1 = Resistor [tolerance=±5% power=0.25W resistance=1k package=THT]
  Power_plug1 = Power plug
  J1 = female pin header, 10 pins [form="♀ (female)"]
  J2 = female pin header, 10 pins [form="♀ (female)"]
  R2 = Resistor [tolerance=±5% power=0.25W resistance=220 package=THT]
  J3 = male pin header, 4 pins [form="♂ (male)"]
  R3 = Resistor [tolerance=±5% power=0.25W resistance=1k package=THT]

nets:
  N1: Part1.A0, R1.Pin_0
  N2: Part1.A1, U1.TXD
  N3: Part1.A5/SCL, LCD2.RX
  N4: Part1.D8, J1.pin6
  N5: Part1.D9_PWM, J1.pin7
  N6: Part1.D10_PWM/SS, J1.pin8
  N7: Part1.D11_PWM/MOSI, J3.pin2
  N8: Part1.D12/MISO, J1.pin9
  N9: Part1.D13/SCK, J2.pin4
  N10: Part1.D2, J1.pin1
  N11: Part1.D3_PWM, J1.pin2
  N12: Part1.D4, J1.pin3
  N13: Part1.D5_PWM, J1.pin4
  N14: Part1.D6_PWM, J2.pin9
  N15: Part1.D7, J2.pin10
  N16: Part1.RESET, J2.pin7
  3V3: Part1.3V3, U1.VCC, U1.CH_PD
  5V: Part1.5V, LCD2.VDD
  GND: Part1.GND, LCD2.GND, U1.GND, Power_plug1.GND, J2.pin8, R2.Pin_1, R3.Pin_0
  VIN: Part1.VIN, Power_plug1.VCC
  N17: U1.RXD, R1.Pin_1
  N18: J2.pin6, R2.Pin_0
  N19: J3.pin1, R3.Pin_1

custom parts:
  Serial Enabled 16x2 LCD - Black on Green 5V: This is the latest evolution of our serial LCD. Included on a single board is a 16x2 LCD and an embedded circuit based around a PIC 16F88. The on-board PIC takes a TTL serial input and prints the characters it receives onto the LCD. The installed firmware also allows for a number of special commands so you can clear the screen, adjust the backlight brightness, turn the display on/off, and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
  ESP8266 ESP-01 Upgraded WiFi Module: Upgraded Version ESP-01,all Flash are upgraded to 1M byte.Also support Cloud service remote transmission.
